# Fritzing sketch protoboard (saved by Fritzing 0.9.10b)

parts:
  Mod1 = Nano-V3-0-IO-Expansion-Adapter
  Part1 = Arduino Nano (Rev3.0)
  M1 = fc-51 [package=THT]
  M2 = fc-51 [package=THT]
  M3 = Dagu DGServo 9g (Top view) [part_number=RS001B]
  M4 = Dagu DGServo 9g (Top view) [part_number=RS001B]
  M5 = fc-51 [package=THT]

nets:
  N1: Mod1.RST, Part1.RESET
  VCC: Mod1.VCC, Part1.5V, M1.pin3, M2.pin3, M3.vcc, M4.vcc, M5.pin3
  GND: Mod1.GND, Part1.GND, M1.pin2, M2.pin2, M3.gnd, M4.gnd, M5.pin2
  VIN: Mod1.VIN, Part1.VIN
  N2: Mod1.A0, Part1.A0
  N3: Mod1.A1, Part1.A1
  N4: Mod1.A2, Part1.A2
  N5: Mod1.A3, Part1.A3
  N6: Mod1.A6, Part1.A6
  N7: Mod1.A7, Part1.A7
  N8: Mod1.D13/SCK, Part1.D13/SCK
  N9: Mod1.NC, Part1.3V3
  N10: Mod1.AREF, Part1.AREF
  N11: Mod1.A4/SDA, Part1.A4
  N12: Mod1.A5/SCL, Part1.A5
  N13: Mod1.D12/MISO, Part1.D12/MISO, M2.pin1
  N14: Mod1.D11_PWM/MOSI, Part1.D11/MOSI, M1.pin1
  N15: Mod1.D10_PWM/SS, Part1.D10
  N16: Mod1.D9_PWM, Part1.D9, M5.pin1
  N17: Mod1.D8, Part1.D8
  N18: Mod1.D7, Part1.D7
  N19: Mod1.D6_PWM, Part1.D6
  N20: Mod1.D5_PWM, Part1.D5
  N21: Mod1.D4, Part1.D4
  N22: Mod1.D3_PWM, Part1.D3
  N23: Mod1.D2, Part1.D2
  N24: Mod1.D0/RX#64, Mod1.D1/TX#129, Part1.D0/RX
  N25: Mod1.D1/TX#65, Mod1.D0/RX#128, Part1.D1/TX

custom parts:
  Nano-V3-0-IO-Expansion-Adapter: Nano V3.0 IO Expansion Adapter Shield. Note pcb view has been supressed as not useful. You can drag a Nano over the Nano connectors and it will connect and appear in schematic (although at present due to a bug, routing will not show as complete in breadboard).
